# Fritzing sketch Schema (saved by Fritzing 0.9.3b)
breadboards: 2

parts:
  LED1 = smd LED [color="Red (635nm)" package="1206 [SMD]"]
  R3 = Resistor [tolerance=±5% resistance=220 package="0603 [SMD]"]
  Part1 = Arduino Uno (Rev3)
  Part2 = KY-006 Passive Buzzer Module [package="Breakout board"]
  HC-SR04_Sensor_1 = HC-SR04 Ultrasonic Distance Sensor

nets:
  N1: LED1.cathode, Part1.D7, Part2.-
  N2: LED1.anode, R3.Pin_1
  N3: Part1.D8, HC-SR04_Sensor_1.ECHO
  N4: Part1.D9_PWM, HC-SR04_Sensor_1.TRIG
  N5: Part1.D6_PWM, Part2.S
  5V: Part1.5V, HC-SR04_Sensor_1.VCC
  GND: Part1.GND, HC-SR04_Sensor_1.GND

custom parts:
  KY-006 Passive Buzzer Module: Passive Piezoelectric Buzzer Module Keyes KY-006, it can produce a range of sound tones depending on the input frequency.
